# Fritzing sketch Lightsaber Sender (saved by Fritzing 0.9.3b)

parts:
  MPU-6050 = MPU-6050 Board GY-521 [form="♀ (female)" package=THT]
  U1 = ESP8266 WiFi Module [part_number=ESP8266]
  Power_plug1 = Power plug

nets:
  3.3V: MPU-6050.pin1, U1.VCC, U1.CH_PD, Power_plug1.VCC
  GND: MPU-6050.pin2, MPU-6050.pin7, U1.GND, Power_plug1.GND
  N1: MPU-6050.pin3, U1.GPIO_2
  N2: MPU-6050.pin4, U1.GPIO_0

notes:
  3.3V regulated
  <--- MPU-6050 Y-axis = Lightsaber axis --->
  VCC
  GND
  SCL
  SDA
  XDA
  XCL
  AD0
  INT
  150mA min

custom parts:
  MPU-6050 Board GY-521: Acelerometro y Giroscopio MPU-6050 Board GY-521
  ESP8266 WiFi Module: Generic WiFi Module based on the ESP8266 with onboard PCB antenna and UART communications
