# Fritzing sketch Syntherrupter Complete Fritzing (saved by Fritzing 0.9.5d)

parts:
  X6 = M10X2 [package=2x10_lock]
  X7 = M10X2 [package=2x10_lock]
  X8 = M10X2 [package=2x10_lock]
  X9 = M10X2 [package=2x10_lock]
  Q1 = NPN-Transistor [package="TO92 [THT]"]
  TX1 = LED - 5mm [color="Infrared (940nm)" package="5 mm [THT]"]
  R1 = Resistor [tolerance=±5% resistance=60 package=THT]
  R2 = Resistor [tolerance=±5% resistance=560 package=THT]
  Q2 = NPN-Transistor [package="TO92 [THT]"]
  TX2 = LED - 5mm [color="Infrared (940nm)" package="5 mm [THT]"]
  R3 = Resistor [tolerance=±5% resistance=60 package=THT]
  R4 = Resistor [tolerance=±5% resistance=560 package=THT]
  Q3 = NPN-Transistor [package="TO92 [THT]"]
  TX3 = LED - 5mm [color="Infrared (940nm)" package="5 mm [THT]"]
  R5 = Resistor [tolerance=±5% resistance=60 package=THT]
  R6 = Resistor [tolerance=±5% resistance=560 package=THT]
  Q6 = NPN-Transistor [package="TO92 [THT]"]
  Q5 = NPN-Transistor [package="TO92 [THT]"]
  Q4 = NPN-Transistor [package="TO92 [THT]"]
  TX4 = LED - 5mm [color="Infrared (940nm)" package="5 mm [THT]"]
  TX5 = LED - 5mm [color="Infrared (940nm)" package="5 mm [THT]"]
  TX6 = LED - 5mm [color="Infrared (940nm)" package="5 mm [THT]"]
  R9 = Resistor [tolerance=±5% resistance=60 package=THT]
  R7 = Resistor [tolerance=±5% resistance=60 package=THT]
  R11 = Resistor [tolerance=±5% resistance=60 package=THT]
  R12 = Resistor [tolerance=±5% resistance=560 package=THT]
  R10 = Resistor [tolerance=±5% resistance=560 package=THT]
  R8 = Resistor [tolerance=±5% resistance=560 package=THT]
  DIN1 = DIN-5 jack (MIDI) [package=THT]
  IC1 = 6n137 Optocoupler [package="DIP (Dual Inline) [THT]"]
  R13 = Resistor [tolerance=±5% resistance=6.8k package=THT]
  D2 = Schottky Diode [part_number=1N4148 package="300 mil [THT]"]
  R14 = Resistor [tolerance=±5% resistance=220 package=THT]
  U1 = ESP8266 WiFi Module [part_number=ESP8266]
  JP1 = female pin header, 4 pins [form="♀ (female)"]
  S1 = Toggle Switch [package=THT]

nets:
  3.3V: X6.1, X8.1
  5V/NX_5V_(Red): X6.2, X8.2, R1.Pin_0, R3.Pin_0, R5.Pin_0, R9.Pin_0, R7.Pin_0, R11.Pin_0, IC1.Ve, IC1.Vcc, R13.Pin_0, U1.VCC, U1.CH_PD, JP1.pin4
  PD2: X6.3, R4.Pin_0
  GND/NX_GND_(Black): X6.4, X7.2, X8.4, X9.2, Q1.E, Q2.E, Q3.E, Q6.E, Q5.E, Q4.E, DIN1.GND, IC1.GND, U1.GND, JP1.pin1, S1.L2
  PD0: X6.5, X9.14, R2.Pin_0
  PB4: X6.6
  PP0: X6.7
  PB5: X6.8
  PD5: X6.9
  PK0: X6.10
  PD4: X6.11
  PK1: X6.12
  PQ0: X6.13
  PK2: X6.14
  PP4: X6.15
  PK3: X6.16
  PN5: X6.17
  NX_TX_(Blue)/PA4: X6.18, JP1.pin2
  PN4: X6.19
  NX_RX_(Yellow)/PA5: X6.20, JP1.pin3
  PG1: X7.1
  PK4: X7.3
  PM7: X7.4
  PK5: X7.5
  PP5: X7.6
  PM0: X7.7, R6.Pin_0
  PA7: X7.8, U1.RXD
  PM1: X7.9
  !RST: X7.10, X9.10
  PM2: X7.11, R8.Pin_0
  PA3/PQ2: X7.12
  PH0: X7.13
  PA2/PQ3: X7.14
  PH1: X7.15
  PP3: X7.16
  PK6: X7.17
  PQ1: X7.18
  PK7: X7.19
  PM6: X7.20, R12.Pin_0
  PE4: X8.3
  PC4: X8.5, IC1.Vo, R13.Pin_1
  PE0: X8.6
  PC5: X8.7
  PE1: X8.8
  PC6: X8.9
  PE2: X8.10
  PE5: X8.11
  PE3: X8.12
  PD3: X8.13
  PD7: X8.14
  PC7: X8.15
  PA6: X8.16, U1.TXD
  PB2: X8.17
  PM4: X8.18, R10.Pin_0
  PB3: X8.19
  PM5: X8.20
  PF1: X9.1
  PF2: X9.3
  PM3: X9.4
  PF3: X9.5
  PH3: X9.6
  PG0: X9.7
  PH2: X9.8
  PL4: X9.9
  PL5: X9.11
  PD1: X9.12
  PL0: X9.13
  PL1: X9.15
  PN2: X9.16
  PL2: X9.17
  PN3: X9.18
  PL3: X9.19
  PP2: X9.20
  N1: Q1.B, R2.Pin_1
  N2: Q1.C, TX1.cathode
  N3: TX1.anode, R1.Pin_1
  N4: Q2.B, R4.Pin_1
  N5: Q2.C, TX2.cathode
  N6: TX2.anode, R3.Pin_1
  N7: Q3.B, R6.Pin_1
  N8: Q3.C, TX3.cathode
  N9: TX3.anode, R5.Pin_1
  N10: Q6.B, R12.Pin_1
  N11: Q6.C, TX6.cathode
  N12: Q5.B, R10.Pin_1
  N13: Q5.C, TX5.cathode
  N14: Q4.B, R8.Pin_1
  N15: Q4.C, TX4.cathode
  N16: TX4.anode, R7.Pin_1
  N17: TX5.anode, R9.Pin_1
  N18: TX6.anode, R11.Pin_1
  N19: DIN1.5, IC1.Vf-, D2.anode
  N20: DIN1.4, R14.Pin_0
  N21: IC1.Vf+, D2.cathode, R14.Pin_1
  N22: U1.GPIO_2, S1.COM

notes:
  1-6 Outputs
  Tiva TM4C1294XL Microcontroller
  Nextion
  MIDI In
  Lightsabers Receiver
  ESP8266 Module should be removable.
  Normal operation
  Flashing

custom parts:
  6n137 Optocoupler: 6n137 fast Optocoupler. With 8 pins on a 300mil dual inline package (DIP) footprint. Ve is strobe input. Output is inverting.
  ESP8266 WiFi Module: Generic WiFi Module based on the ESP8266 with onboard PCB antenna and UART communications
